// Logisim project 4_bit_load_only_reg.circ as structural Verilog: 1 circuit, main circuit main
module main (
  input  CLK_for_library,
  input  [3:0] OutFlag,
  input  Enable,
  input  Reset,
  output [3:0] Cin
);

  wire and_1_out, CLK_out, or_1_out;

  Hex_Digit_Display hex_digit_display_1 (.value(OutFlag));  // open: dp
  Clock CLK (.out(CLK_out));
  or or_1 (or_1_out, CLK_for_library, CLK_out);
  and and_1 (and_1_out, Enable, Reset);
  D_Flip_Flop Z (.clk(or_1_out), .D(OutFlag[3]), .Q(Cin[3]), .en(Enable), .reset(and_1_out));  // open: Qn, preset
  D_Flip_Flop C (.clk(or_1_out), .D(OutFlag[2]), .Q(Cin[2]), .en(Enable), .reset(and_1_out));  // open: Qn, preset
  D_Flip_Flop N (.clk(or_1_out), .D(OutFlag[1]), .Q(Cin[1]), .en(Enable), .reset(and_1_out));  // open: Qn, preset
  D_Flip_Flop O (.clk(or_1_out), .D(OutFlag[0]), .Q(Cin[0]), .en(Enable), .reset(and_1_out));  // open: Qn, preset
  Hex_Digit_Display hex_digit_display_2 (.value(Cin));  // open: dp

  // Notes on the sheet:
  //   Hex Output
endmodule
