// Logisim project FINAL.circ as structural Verilog: 1 circuit, main circuit main
module main (
  input  CLK,
  output [3:0] ALU_Z_C_N_O
);

  wire clock_1_out, IR_ENABLE, IR_L_H_prime, MuxCsel, not_1_out, or_1_out, Ram_CLEAR, Ram_LOAD, Ram_STORE;
  wire [1:0] IR_FUNSEL, MuxAsel, MuxBsel, PC_Ar_Funsel, PC_Ar_OutselC, PC_Ar_OutselD, R0_R3_Funsel,
       R0_R3_OutselA, R0_R3_OutselB;
  wire [2:0] PC_Ar_Regsel;
  wire [3:0] ALU_FUNSEL, main_1_outa, main_1_outa_2, main_1_outb, main_1_outb_2, main_3_out_d,
       main_3_out_d_2, main_4_outflag, multiplexer_1_out, multiplexer_1_out_2, R0_R3_Regsel;
  wire [7:0] main_3_out_c, main_4_outalu, multiplexer_2_out, multiplexer_3_out, ram_1_data;
  wire [15:0] Instructions;

  Hex_Digit_Display hex_digit_display_1 (.value(main_1_outa_2));  // open: dp
  Hex_Digit_Display hex_digit_display_2 (.value(multiplexer_1_out_2));  // open: dp
  Hex_Digit_Display hex_digit_display_3 (.value(main_1_outb_2));  // open: dp
  Hex_Digit_Display hex_digit_display_4 (.value(main_1_outa));  // open: dp
  Hex_Digit_Display hex_digit_display_5 (.value(multiplexer_1_out));  // open: dp
  Hex_Digit_Display hex_digit_display_6 (.value(Instructions[7:4]));  // open: dp
  Hex_Digit_Display hex_digit_display_7 (.value(main_1_outb));  // open: dp
  Multiplexer #(.select(2), .width(8), .enable("false")) multiplexer_1 (
    .in0(Instructions[7:0]), .in1(ram_1_data), .in2(main_3_out_c), .in3(main_4_outalu),
    .out({multiplexer_1_out_2, multiplexer_1_out}), .sel(MuxAsel));
  Hex_Digit_Display hex_digit_display_8 (.value(Instructions[3:0]));  // open: dp
  part2a_main main_1 (
    ._8_bit_IN({multiplexer_1_out_2, multiplexer_1_out}), .RegSel(R0_R3_Regsel), .Clock(or_1_out),
    .FunSel(R0_R3_Funsel), .OutSelA(R0_R3_OutselA), .OutSelB(R0_R3_OutselB),
    .OutA({main_1_outa_2, main_1_outa}), .OutB({main_1_outb_2, main_1_outb}));
  not not_1 (not_1_out, IR_L_H_prime);
  Multiplexer #(.width(8), .enable("false")) multiplexer_2 (
    .in0(main_3_out_c), .in1({main_1_outa_2, main_1_outa}), .out(multiplexer_2_out), .sel(MuxCsel));
  Multiplexer #(.select(2), .width(8), .enable("false")) multiplexer_3 (
    .in0(multiplexer_3_out), .in1(Instructions[7:0]), .in2(ram_1_data), .in3(main_4_outalu),
    .out(multiplexer_3_out), .sel(MuxBsel));
  Part2c_main main_2 (
    .FunSel(IR_FUNSEL), .\Input_Pın___8_bit (ram_1_data), .L_prime_H(not_1_out), .ENABLE(IR_ENABLE),
    .Output(Instructions), .Clock(or_1_out));  // open: out_7
  Hex_Digit_Display hex_digit_display_9 (.value(main_3_out_d));  // open: dp
  Hex_Digit_Display hex_digit_display_10 (.value(main_3_out_d_2));  // open: dp
  part2b_main main_3 (
    ._8_bit_IN(multiplexer_3_out), .RegSel(PC_Ar_Regsel), .Clock(or_1_out), .FunSel(PC_Ar_Funsel),
    .OutSelC(PC_Ar_OutselC), .OutSelD(PC_Ar_OutselD), .OUT_C(main_3_out_c),
    .OUT_D({main_3_out_d_2, main_3_out_d}));
  Hex_Digit_Display hex_digit_display_11 (.value(main_3_out_c[7:4]));  // open: dp
  Hex_Digit_Display hex_digit_display_12 (.value(main_4_outalu[7:4]));  // open: dp
  corg_P2_main main_4 (
    .A(multiplexer_2_out), .B({main_1_outb_2, main_1_outb}), .FunSel(ALU_FUNSEL), .OutALU(main_4_outalu),
    .Cin(ALU_Z_C_N_O[2]), .OutFlag(main_4_outflag));
  Hex_Digit_Display hex_digit_display_13 (.value(main_3_out_c[3:0]));  // open: dp
  Hex_Digit_Display hex_digit_display_14 (.value(main_4_outalu[3:0]));  // open: dp
  _4_bit_load_only_reg_main main_5 (
    .Cin(ALU_Z_C_N_O), .Enable(1'b1), .CLK_for_library(or_1_out), .OutFlag(main_4_outflag));  // open: Reset
  Hex_Digit_Display hex_digit_display_15 (.value(ram_1_data[7:4]));  // open: dp
  Hex_Digit_Display hex_digit_display_16 (.value(ram_1_data[3:0]));  // open: dp
  or or_1 (or_1_out, clock_1_out, CLK);
  RAM #(.bus("separate")) ram_1 (
    .addr({main_3_out_d_2, main_3_out_d}), .din(main_4_outalu), .data(ram_1_data), .str(Ram_STORE),
    .sel(1'b1), .clk(or_1_out), .ld(Ram_LOAD), .clr(Ram_CLEAR));
  Clock clock_1 (.out(clock_1_out));
  Cunit_main main_6 (
    .INSTRUCTIONS(Instructions), .ZERO_FLAG_INPUT(ALU_Z_C_N_O[3]), .CLOCK(or_1_out),
    .RX_regsel(R0_R3_Regsel), .RX_funsel(R0_R3_Funsel), .OUTA(R0_R3_OutselA), .OUTB(R0_R3_OutselB),
    .ALU_FUN(ALU_FUNSEL), .PX_regsel(PC_Ar_Regsel), .PX_funsel(PC_Ar_Funsel), .OUTC(PC_Ar_OutselC),
    .OUTD(PC_Ar_OutselD), .RAM_STR(Ram_STORE), .RAM_LD(Ram_LOAD), .MUXA(MuxAsel), .MUXB(MuxBsel),
    .MUXC(MuxCsel), .IR_ENABLE(IR_ENABLE), .IR_funsel(IR_FUNSEL), .IR_L_H_prime(IR_L_H_prime));

  // Other names for the same wires on the sheet: Z_FLAG = ALU_Z_C_N_O[3]

  // Notes on the sheet:
  //   OutA
  //   MuxAOut
  //   IROut (0-7)
  //   OutB
  //   Adress Reg OutD
  //   Adress Reg OutC
  //   OutALU
  //   Memory Output
endmodule
