// Logisim project part1-8bit.circ as structural Verilog: 1 circuit, main circuit main
module main (
  input  [1:0] FunSel,
  input  [7:0] _8_bit_Input,
  input  CLK__do_not_use,
  input  Enable,
  output [7:0] _8_bit_Output,
  output out_6
);

  wire and_1_out, and_2_out, and_3_out, and_4_out, and_5_out, and_6_out, and_7_out, and_8_out, and_9_out,
       and_10_out, and_11_out, and_12_out, and_13_out, and_14_out, and_15_out, and_16_out, and_17_out,
       and_18_out, CLK_out, decoder_1_out0, decoder_1_out1, decoder_1_out2, decoder_1_out3, or_1_out,
       or_2_out, or_3_out, or_4_out, or_5_out, or_6_out, or_7_out, or_8_out, or_9_out, or_10_out, or_11_out;
  wire [7:0] adder_1_out, multiplexer_1_out;

  Decoder #(.select(2), .enable("false")) decoder_1 (
    .out0(decoder_1_out0), .out1(decoder_1_out1), .out2(decoder_1_out2), .out3(decoder_1_out3), .sel(FunSel));
  or or_1 (or_1_out, decoder_1_out2, decoder_1_out3);
  and and_1 (and_1_out, _8_bit_Input[7], decoder_1_out1);
  and and_2 (and_2_out, _8_bit_Input[6], decoder_1_out1);
  and and_3 (and_3_out, _8_bit_Input[5], decoder_1_out1);
  and and_4 (and_4_out, _8_bit_Input[4], decoder_1_out1);
  and and_5 (and_5_out, _8_bit_Input[3], decoder_1_out1);
  and and_6 (and_6_out, _8_bit_Input[2], decoder_1_out1);
  and and_7 (and_7_out, _8_bit_Input[1], decoder_1_out1);
  and and_8 (and_8_out, _8_bit_Input[0], decoder_1_out1);
  Hex_Digit_Display hex_digit_display_1 (.value(_8_bit_Input[7:4]));  // open: dp
  Hex_Digit_Display hex_digit_display_2 (.value(_8_bit_Input[3:0]));  // open: dp
  and and_9 (and_9_out, adder_1_out[7], or_1_out);
  and and_10 (and_10_out, adder_1_out[6], or_1_out);
  and and_11 (and_11_out, adder_1_out[5], or_1_out);
  and and_12 (and_12_out, adder_1_out[4], or_1_out);
  and and_13 (and_13_out, or_1_out, adder_1_out[3]);
  and and_14 (and_14_out, or_1_out, adder_1_out[2]);
  and and_15 (and_15_out, or_1_out, adder_1_out[1]);
  and and_16 (and_16_out, adder_1_out[0], or_1_out);
  or or_2 (or_2_out, and_1_out, and_9_out);
  or or_3 (or_3_out, and_2_out, and_10_out);
  or or_4 (or_4_out, and_3_out, and_11_out);
  or or_5 (or_5_out, and_4_out, and_12_out);
  or or_6 (or_6_out, and_5_out, and_13_out);
  or or_7 (or_7_out, and_6_out, and_14_out);
  or or_8 (or_8_out, and_7_out, and_15_out);
  or or_9 (or_9_out, and_8_out, and_16_out);
  Clock CLK (.out(CLK_out));
  or or_10 (or_10_out, CLK__do_not_use, CLK_out);
  and and_17 (and_17_out, or_10_out, decoder_1_out0);
  and and_18 (and_18_out, Enable, and_17_out);
  Multiplexer #(.width(8)) multiplexer_1 (
    .in0({8{1'b1}}), .in1(8'h1), .out(multiplexer_1_out), .sel(decoder_1_out2), .en(or_11_out));
  or or_11 (or_11_out, decoder_1_out2, decoder_1_out3);
  D_Flip_Flop d_ff_1 (
    .clk(or_10_out), .D(or_2_out), .Q(_8_bit_Output[7]), .en(Enable), .reset(and_18_out));  // open: Qn, preset
  D_Flip_Flop d_ff_2 (
    .clk(or_10_out), .D(or_3_out), .Q(_8_bit_Output[6]), .en(Enable), .reset(and_18_out));  // open: Qn, preset
  D_Flip_Flop d_ff_3 (
    .clk(or_10_out), .D(or_4_out), .Q(_8_bit_Output[5]), .en(Enable), .reset(and_18_out));  // open: Qn, preset
  D_Flip_Flop d_ff_4 (
    .clk(or_10_out), .D(or_5_out), .Q(_8_bit_Output[4]), .en(Enable), .reset(and_18_out));  // open: Qn, preset
  D_Flip_Flop d_ff_5 (
    .clk(or_10_out), .D(or_6_out), .Q(_8_bit_Output[3]), .en(Enable), .reset(and_18_out));  // open: Qn, preset
  D_Flip_Flop d_ff_6 (
    .clk(or_10_out), .D(or_7_out), .Q(_8_bit_Output[2]), .en(Enable), .reset(and_18_out));  // open: Qn, preset
  D_Flip_Flop d_ff_7 (
    .clk(or_10_out), .D(or_8_out), .Q(_8_bit_Output[1]), .en(Enable), .reset(and_18_out));  // open: Qn, preset
  D_Flip_Flop d_ff_8 (
    .clk(or_10_out), .D(or_9_out), .Q(_8_bit_Output[0]), .en(Enable), .reset(and_18_out));  // open: Qn, preset
  Adder adder_1 (.a(_8_bit_Output), .b(multiplexer_1_out), .out(adder_1_out), .cout(out_6));  // open: cin
  Hex_Digit_Display hex_digit_display_3 (.value(_8_bit_Output[7:4]));  // open: dp
  Hex_Digit_Display hex_digit_display_4 (.value(_8_bit_Output[3:0]));  // open: dp

  // Notes on the sheet:
  //   Hex Output
endmodule
