// Logisim project corg_P2.circ as structural Verilog: 1 circuit, main circuit main
module main (
  input  [7:0] A,
  input  [7:0] B,
  input  Cin,
  input  [3:0] FunSel,
  output [7:0] OutALU,
  output [3:0] OutFlag
);

  wire adder_2_cout, adder_3_cout, adder_4_cout, and_2_out, and_3_out, and_4_out, ASL_overflow, C_q,
       clock_out, CSL_carry, CSL_overflow, CSR_carry, CSR_overflow, LSL_carry, LSR_carry, N_q, O_q, undriven,
       xor_2_out, xor_3_out, xor_4_out, xor_5_out, xor_6_out, xor_7_out, Z_q;
  wire [7:0] adder_1_out, adder_2_out, adder_3_out, adder_4_out, and_1_out, ASL_output, ASR_output,
       CSL_output, CSR_output, LSL_output, LSR_output, not_1_out, not_2_out, not_3_out, or_1_out, xor_1_out;

  arit_shift_left_main ASL (.INPUT(A), .OUTPUT(ASL_output), .OVERFLOW(ASL_overflow));
  arit_shift_right_main ASR (.INPUT(A), .OUTPUT(ASR_output));
  circ_shift_left_main CSL (.INPUT(A), .OUTPUT(CSL_output), .CARRY(CSL_carry), .OVERFLOW(CSL_overflow));
  circ_shift_right_main CSR (.INPUT(A), .OUTPUT(CSR_output), .CARRY(CSR_carry), .OVERFLOW(CSR_overflow));
  logic_shift_left_main LSL (.INPUT(A), .OUTPUT(LSL_output), .CARRY(LSL_carry));
  logic_shift_right_main LSR (.INPUT(A), .OUTPUT(LSR_output), .CARRY(LSR_carry));
  assign xor_1_out = B ^ A;  // XOR_Gate xor_1, 8 bits wide
  assign or_1_out = B | A;  // OR_Gate or_1, 8 bits wide
  assign and_1_out = B & A;  // AND_Gate and_1, 8 bits wide
  assign not_1_out = ~B;  // NOT_Gate not_1, 8 bits wide
  Adder adder_1 (.a(not_1_out), .b(8'h1), .out(adder_1_out));  // open: cin, cout
  Adder adder_2 (.a(A), .b(B), .out(adder_2_out), .cin(Cin), .cout(adder_2_cout));
  Adder adder_3 (.a(A), .b(adder_1_out), .out(adder_3_out), .cout(adder_3_cout));  // open: cin
  Adder adder_4 (.a(A), .b(B), .out(adder_4_out), .cout(adder_4_cout));  // open: cin
  assign not_2_out = ~B;  // NOT_Gate not_2, 8 bits wide
  assign not_3_out = ~A;  // NOT_Gate not_3, 8 bits wide
  xor xor_2 (xor_2_out, A[7], adder_4_out[7]);
  xor xor_3 (xor_3_out, adder_4_out[7], B[7]);
  xor xor_4 (xor_4_out, A[7], adder_2_out[7]);
  xor xor_5 (xor_5_out, adder_2_out[7], B[7]);
  xor xor_6 (xor_6_out, A[7], adder_3_out[7]);
  xor xor_7 (xor_7_out, adder_3_out[7], adder_1_out[7]);
  and and_2 (and_2_out, xor_2_out, xor_3_out);
  and and_3 (and_3_out, xor_4_out, xor_5_out);
  and and_4 (and_4_out, xor_6_out, xor_7_out);
  Multiplexer #(.select(4), .width(8)) multiplexer_1 (
    .in0(A), .in1(B), .in2(not_3_out), .in3(not_2_out), .in4(adder_4_out), .in5(adder_2_out),
    .in6(adder_3_out), .in7(and_1_out), .in8(or_1_out), .in9(xor_1_out), .in10(LSL_output),
    .in11(LSR_output), .in12(ASL_output), .in13(ASR_output), .in14(CSL_output), .in15(CSR_output),
    .out(OutALU), .sel(FunSel));  // open: en
  Multiplexer #(.select(4)) multiplexer_2 (
    .in0(A[7]), .in1(B[7]), .in2(not_3_out[7]), .in3(not_2_out[7]), .in4(adder_4_out[7]),
    .in5(adder_2_out[7]), .in6(adder_3_out[7]), .in7(and_1_out[7]), .in8(or_1_out[7]), .in9(xor_1_out[7]),
    .in10(LSL_output[7]), .in11(LSR_output[7]), .in12(ASL_output[7]), .in14(CSL_output[7]),
    .in15(CSR_output[7]), .out(OutFlag[1]), .sel(FunSel));  // open: in13, en
  Multiplexer #(.select(4)) multiplexer_3 (
    .in4(adder_4_cout), .in5(adder_2_cout), .in6(adder_3_cout), .in10(LSL_carry), .in11(LSR_carry),
    .in14(CSL_carry), .in15(CSR_carry), .out(OutFlag[2]), .sel(FunSel));  // open: in0, in1, in2, in3, in7, in8, in9, in12, in13, en
  Multiplexer #(.select(4)) multiplexer_4 (
    .in4(and_2_out), .in5(and_3_out), .in6(and_4_out), .in12(ASL_overflow), .in14(CSL_overflow),
    .in15(CSR_overflow), .out(OutFlag[0]), .sel(FunSel));  // open: in0, in1, in2, in3, in7, in8, in9, in10, in11, in13, en
  Comparator comparator_1 (.a(OutALU), .b({8{1'b0}}), .eq(OutFlag[3]));  // open: gt, lt
  Clock clock (.out(clock_out));
  D_Flip_Flop Z (.clk(clock_out), .D(OutFlag[3]), .Q(Z_q), .en(undriven));  // open: Qn, preset, reset
  D_Flip_Flop C (.clk(clock_out), .D(OutFlag[2]), .Q(C_q), .en(undriven));  // open: Qn, preset, reset
  D_Flip_Flop N (.clk(clock_out), .D(OutFlag[1]), .Q(N_q), .en(undriven));  // open: Qn, preset, reset
  D_Flip_Flop O (.clk(clock_out), .D(OutFlag[0]), .Q(O_q), .en(undriven));  // open: Qn, preset, reset
endmodule
