// Logisim project logic shift left.circ as structural Verilog: 1 circuit, main circuit main
module main (
  input  [7:0] INPUT,
  output CARRY,
  output [7:0] OUTPUT
);


  assign CARRY = INPUT[7];
  assign OUTPUT = {INPUT[6:0], 1'b0};
endmodule
