// Logisim project logic shift right.circ as structural Verilog: 1 circuit, main circuit main
module main (
  input  [7:0] INPUT,
  output CARRY,
  output [7:0] OUTPUT
);


  assign CARRY = INPUT[0];
  assign OUTPUT = {1'b0, INPUT[7:1]};
endmodule
