// Logisim project Control _Unit.circ as structural Verilog: 1 circuit, main circuit main
module main (
  input  [15:0] Instructions,
  input  Z_Flag,
  input  Clock,
  output [1:0] MUXA,
  output [1:0] MUXB,
  output MUXC,
  output [3:0] R0_R3_regsel,
  output [2:0] PC_AR_SP_regsel,
  output L_H_prime,
  output [1:0] R0_R3_funsel,
  output [1:0] PC_AR_SP_funsel,
  output IR_Enable,
  output [1:0] OutAsel,
  output [1:0] OutCsel,
  output [1:0] IR_FUNSEL,
  output [1:0] OutBsel,
  output [1:0] OutDsel,
  output [3:0] Alu_Funsel,
  output RAM_write,
  output RAM_read
);

  wire and_1_out, and_2_out, and_3_out, and_4_out, and_5_out, and_6_out, and_7_out, and_8_out, and_9_out,
       and_10_out, and_11_out, and_12_out, and_13_out, and_14_out, and_15_out, and_16_out, and_17_out,
       and_18_out, and_19_out, and_20_out, and_21_out, and_22_out, and_23_out, and_24_out, and_25_out,
       and_26_out, and_27_out, and_28_out, and_29_out, and_30_out, and_31_out, and_32_out, and_33_out,
       and_34_out, and_35_out, and_36_out, and_37_out, and_38_out, and_39_out, and_40_out, and_41_out,
       and_42_out, and_43_out, and_44_out, and_45_out, and_46_out, and_47_out, and_48_out, and_49_out,
       and_50_out, and_51_out, and_52_out, and_53_out, and_54_out, and_55_out, and_56_out, and_57_out,
       and_58_out, and_59_out, and_60_out, and_61_out, and_62_out, and_63_out, and_64_out, and_65_out,
       and_66_out, and_67_out, and_68_out, and_69_out, and_70_out, and_71_out, and_72_out, and_73_out,
       and_74_out, and_75_out, and_76_out, and_77_out, and_78_out, and_79_out, and_80_out, and_81_out,
       and_82_out, and_83_out, and_84_out, and_85_out, and_86_out, and_87_out, and_88_out, and_89_out,
       and_90_out, and_91_out, and_92_out, and_93_out, and_94_out, and_95_out, and_96_out, and_97_out,
       and_98_out, and_99_out, and_100_out, and_101_out, and_102_out, and_103_out, and_104_out, and_105_out,
       and_106_out, and_107_out, and_108_out, and_109_out, and_110_out, and_111_out, and_112_out,
       and_113_out, and_114_out, and_115_out, and_116_out, and_117_out, and_118_out, and_119_out,
       and_120_out, and_121_out, and_122_out, and_123_out, and_124_out, and_125_out, and_126_out,
       and_127_out, and_128_out, and_129_out, and_130_out, and_131_out, and_132_out, and_133_out,
       and_134_out, and_135_out, and_136_out, and_137_out, and_138_out, and_139_out, and_140_out,
       and_141_out, and_142_out, and_143_out, and_144_out, and_145_out, and_146_out, and_147_out,
       and_148_out, and_149_out, and_150_out, and_151_out, and_152_out, and_153_out, and_154_out,
       and_155_out, and_156_out, and_157_out, and_158_out, and_159_out, and_160_out, and_161_out,
       and_162_out, and_163_out, and_164_out, and_165_out, and_166_out, and_167_out, and_168_out,
       and_169_out, and_170_out, and_171_out, and_172_out, and_173_out, and_174_out, and_175_out,
       and_176_out, and_177_out, and_178_out, and_179_out, and_180_out, and_181_out, and_182_out,
       and_183_out, and_184_out, and_185_out, and_186_out, and_187_out, and_188_out, and_189_out,
       and_190_out, and_191_out, and_192_out, and_193_out, and_194_out, and_195_out, and_196_out,
       and_197_out, and_198_out, and_199_out, and_200_out, D0, D1, D2, D3, D4, D5, D5_D6_D9_D10, D6, D7,
       D7_D8, D8, D9, D10, D11, D11_D12_D13, D12, D13, D14, D15, D16, D17, D18, d_ff_1_q, decoder_3_out0,
       decoder_3_out1, not_1_out, or_1_out, or_2_out, or_3_out, or_4_out, or_8_out, or_9_out, or_10_out,
       or_11_out, or_12_out, or_14_out, or_15_out, or_16_out, or_17_out, or_18_out, or_19_out, or_20_out, T0,
       T1, T2, T3, T4, T5, T6, T7, Time_Reset;
  wire [1:0] controlled_buffer_56_out, controlled_buffer_106_out;
  wire [2:0] counter_1_q, or_13_out;

  Counter #(.width(3), .max('h7)) counter_1 (
    .Q(counter_1_q), .clk(Clock), .clr(d_ff_1_q));  // open: load, D, count, carry
  and and_1 (and_1_out, D0, Instructions[8], T2);
  and and_2 (and_2_out, D4, T3);
  and and_3 (and_3_out, D18, T3);
  assign L_H_prime = T0 ? 1'b0 : 1'bz;  // Controlled_Buffer controlled_buffer_1
  assign L_H_prime = T1 ? 1'b1 : 1'bz;  // Controlled_Buffer controlled_buffer_2
  Decoder #(.select(3), .enable("false")) decoder_1 (
    .out0(T0), .out1(T1), .out2(T2), .out3(T3), .out4(T4), .out5(T5), .out6(T6), .out7(T7), .sel(counter_1_q));
  D_Flip_Flop d_ff_1 (.clk(Clock), .D(Time_Reset), .Q(d_ff_1_q), .en(1'b1), .reset(d_ff_1_q));  // open: Qn, preset
  assign RAM_read = or_1_out ? 1'b1 : 1'bz;  // Controlled_Buffer controlled_buffer_3
  or or_1 (or_1_out, T0, T1);
  assign RAM_read = and_1_out ? 1'b1 : 1'bz;  // Controlled_Buffer controlled_buffer_4
  assign RAM_read = and_2_out ? 1'b1 : 1'bz;  // Controlled_Buffer controlled_buffer_5
  assign RAM_read = and_3_out ? 1'b1 : 1'bz;  // Controlled_Buffer controlled_buffer_6
  assign IR_FUNSEL = or_2_out ? 2'b11 : 2'bz;  // Controlled_Buffer controlled_buffer_7
  or or_2 (or_2_out, T0, T1);
  assign IR_Enable = or_3_out ? 1'b1 : 1'bz;  // Controlled_Buffer controlled_buffer_8
  or or_3 (or_3_out, T0, T1);
  Decoder #(.select(5), .enable("false")) decoder_2 (
    .out0(D0), .out1(D1), .out2(D2), .out3(D3), .out4(D4), .out5(D5), .out6(D6), .out7(D7), .out8(D8),
    .out9(D9), .out10(D10), .out11(D11), .out12(D12), .out13(D13), .out14(D14), .out15(D15), .out16(D16),
    .out17(D17), .out18(D18), .sel(Instructions[15:11]));  // open: out19, out20, out21, out22, out23, out24, out25, out26, out27, out28, out29, out30, out31
  and and_4 (and_4_out, D1, Instructions[8], T2);
  and and_5 (and_5_out, D3, ~Instructions[7], T2);  // AND_Gate
  and and_6 (and_6_out, D17, T2);
  or or_4 (or_4_out, and_4_out, and_5_out, and_6_out);
  assign RAM_write = or_4_out ? 1'b1 : 1'bz;  // Controlled_Buffer controlled_buffer_9
  assign RAM_write = not_1_out ? 1'b0 : 1'bz;  // Controlled_Buffer controlled_buffer_10
  not not_1 (not_1_out, or_4_out);
  or or_5 (D11_D12_D13, D11, D12, D13);
  or or_6 (D5_D6_D9_D10, D5, D6, D9, D10);
  or or_7 (D7_D8, D7, D8);
  and and_7 (and_7_out, D0, ~Instructions[8], T2);  // AND_Gate
  and and_8 (and_8_out, D0, Instructions[8], T2);
  and and_9 (and_9_out, D3, Instructions[7], T2);
  and and_10 (and_10_out, D4, ~Instructions[10], T3);  // AND_Gate
  and and_11 (and_11_out, D5_D6_D9_D10, ~Instructions[10], ~Instructions[7], ~Instructions[4], T2);  // AND_Gate
  and and_12 (and_12_out, D5_D6_D9_D10, ~Instructions[10], Instructions[7], ~Instructions[4], T2);  // AND_Gate
  and and_13 (and_13_out, D5_D6_D9_D10, ~Instructions[10], Instructions[7], ~Instructions[4], T3);  // AND_Gate
  and and_14 (and_14_out, D5_D6_D9_D10, Instructions[10], Instructions[7], ~Instructions[4], T2);  // AND_Gate
  and and_15 (and_15_out, D7_D8, ~Instructions[10], ~Instructions[7], T2);  // AND_Gate
  and and_16 (and_16_out, D7_D8, ~Instructions[10], Instructions[7], T2);  // AND_Gate
  and and_17 (and_17_out, D7_D8, Instructions[10], Instructions[7], T2);
  and and_18 (and_18_out, D11_D12_D13, ~Instructions[10], ~Instructions[7], T2);  // AND_Gate
  and and_19 (and_19_out, D11_D12_D13, ~Instructions[10], Instructions[7], T2);  // AND_Gate
  and and_20 (and_20_out, D11_D12_D13, ~Instructions[10], Instructions[7], T3);  // AND_Gate
  and and_21 (and_21_out, D11_D12_D13, Instructions[10], Instructions[7], T2);
  and and_22 (and_22_out, D17, T2);
  assign MUXA = and_7_out ? 2'b00 : 2'bz;  // Controlled_Buffer controlled_buffer_11
  assign MUXA = and_8_out ? 2'b01 : 2'bz;  // Controlled_Buffer controlled_buffer_12
  assign MUXA = and_23_out ? 2'b10 : 2'bz;  // Controlled_Buffer controlled_buffer_13
  and and_23 (and_23_out, D2, Instructions[7], T2);
  assign MUXA = and_24_out ? 2'b11 : 2'bz;  // Controlled_Buffer controlled_buffer_14
  and and_24 (and_24_out, D2, ~Instructions[7], ~Instructions[10], T2);  // AND_Gate
  assign MUXA = and_9_out ? 2'b10 : 2'bz;  // Controlled_Buffer controlled_buffer_15
  assign MUXA = and_10_out ? 2'b01 : 2'bz;  // Controlled_Buffer controlled_buffer_16
  assign MUXA = and_11_out ? 2'b11 : 2'bz;  // Controlled_Buffer controlled_buffer_17
  assign MUXA = and_12_out ? 2'b10 : 2'bz;  // Controlled_Buffer controlled_buffer_18
  assign MUXA = and_13_out ? 2'b11 : 2'bz;  // Controlled_Buffer controlled_buffer_19
  assign MUXA = and_14_out ? 2'b10 : 2'bz;  // Controlled_Buffer controlled_buffer_20
  assign MUXA = and_15_out ? 2'b11 : 2'bz;  // Controlled_Buffer controlled_buffer_21
  assign MUXA = and_16_out ? 2'b10 : 2'bz;  // Controlled_Buffer controlled_buffer_22
  assign MUXA = and_17_out ? 2'b10 : 2'bz;  // Controlled_Buffer controlled_buffer_23
  assign MUXA = and_18_out ? 2'b11 : 2'bz;  // Controlled_Buffer controlled_buffer_24
  assign MUXA = and_19_out ? 2'b10 : 2'bz;  // Controlled_Buffer controlled_buffer_25
  assign MUXA = and_20_out ? 2'b11 : 2'bz;  // Controlled_Buffer controlled_buffer_26
  assign MUXA = and_21_out ? 2'b10 : 2'bz;  // Controlled_Buffer controlled_buffer_27
  assign MUXA = and_22_out ? 2'b10 : 2'bz;  // Controlled_Buffer controlled_buffer_28
  and and_25 (and_25_out, D14, T2);
  and and_26 (and_26_out, D15, Z_Flag, T2);
  and and_27 (and_27_out, D16, ~Z_Flag, T2);  // AND_Gate
  and and_28 (and_28_out, D17, T3);
  and and_29 (and_29_out, D18, T3);
  assign MUXB = and_30_out ? 2'b11 : 2'bz;  // Controlled_Buffer controlled_buffer_29
  and and_30 (and_30_out, D2, Instructions[10], Instructions[7], T2);
  assign MUXB = and_31_out ? 2'b11 : 2'bz;  // Controlled_Buffer controlled_buffer_30
  and and_31 (and_31_out, D2, Instructions[10], ~Instructions[7], T2);  // AND_Gate
  assign MUXB = and_32_out ? 2'b10 : 2'bz;  // Controlled_Buffer controlled_buffer_31
  and and_32 (and_32_out, D4, Instructions[10], T3);
  assign MUXB = and_33_out ? 2'b11 : 2'bz;  // Controlled_Buffer controlled_buffer_32
  and and_33 (and_33_out, D5_D6_D9_D10, Instructions[10], ~Instructions[7], ~Instructions[4], T2);  // AND_Gate
  assign MUXB = and_34_out ? 2'b11 : 2'bz;  // Controlled_Buffer controlled_buffer_33
  and and_34 (and_34_out, D5_D6_D9_D10, Instructions[10], Instructions[7], ~Instructions[4], T2);  // AND_Gate
  assign MUXB = and_35_out ? 2'b11 : 2'bz;  // Controlled_Buffer controlled_buffer_34
  and and_35 (and_35_out, D7_D8, Instructions[10], ~Instructions[7], T2);  // AND_Gate
  assign MUXB = and_36_out ? 2'b11 : 2'bz;  // Controlled_Buffer controlled_buffer_35
  and and_36 (and_36_out, D7_D8, Instructions[10], Instructions[7], T2);
  assign MUXB = and_37_out ? 2'b11 : 2'bz;  // Controlled_Buffer controlled_buffer_36
  and and_37 (and_37_out, D11_D12_D13, Instructions[10], ~Instructions[7], T2);  // AND_Gate
  assign MUXB = and_38_out ? 2'b11 : 2'bz;  // Controlled_Buffer controlled_buffer_37
  and and_38 (and_38_out, D11_D12_D13, Instructions[10], Instructions[7], T2);
  assign MUXB = and_25_out ? 2'b01 : 2'bz;  // Controlled_Buffer controlled_buffer_38
  assign MUXB = and_26_out ? 2'b01 : 2'bz;  // Controlled_Buffer controlled_buffer_39
  assign MUXB = and_27_out ? 2'b01 : 2'bz;  // Controlled_Buffer controlled_buffer_40
  assign MUXB = and_28_out ? 2'b01 : 2'bz;  // Controlled_Buffer controlled_buffer_41
  assign MUXB = and_29_out ? 2'b10 : 2'bz;  // Controlled_Buffer controlled_buffer_42
  assign MUXC = and_39_out ? 1'b0 : 1'bz;  // Controlled_Buffer controlled_buffer_43
  and and_39 (and_39_out, D2, Instructions[10], Instructions[7], T3);
  assign MUXC = and_40_out ? 1'b0 : 1'bz;  // Controlled_Buffer controlled_buffer_44
  and and_40 (and_40_out, D3, Instructions[7], T2);
  assign MUXC = and_41_out ? 1'b1 : 1'bz;  // Controlled_Buffer controlled_buffer_45
  and and_41 (and_41_out, D5_D6_D9_D10, ~Instructions[10], ~Instructions[7], ~Instructions[4], T2);  // AND_Gate
  assign MUXC = and_42_out ? 1'b1 : 1'bz;  // Controlled_Buffer controlled_buffer_46
  and and_42 (and_42_out, D5_D6_D9_D10, ~Instructions[10], Instructions[7], ~Instructions[4], T3);  // AND_Gate
  assign MUXC = and_43_out ? 1'b1 : 1'bz;  // Controlled_Buffer controlled_buffer_47
  and and_43 (and_43_out, D5_D6_D9_D10, Instructions[10], ~Instructions[7], ~Instructions[4], T2);  // AND_Gate
  assign MUXC = and_44_out ? 1'b0 : 1'bz;  // Controlled_Buffer controlled_buffer_48
  and and_44 (and_44_out, D5_D6_D9_D10, Instructions[10], Instructions[7], ~Instructions[4], T2);  // AND_Gate
  assign MUXC = and_45_out ? 1'b1 : 1'bz;  // Controlled_Buffer controlled_buffer_49
  and and_45 (and_45_out, D7_D8, ~Instructions[10], ~Instructions[7], T2);  // AND_Gate
  assign MUXC = and_46_out ? 1'b1 : 1'bz;  // Controlled_Buffer controlled_buffer_50
  and and_46 (and_46_out, D7_D8, Instructions[10], ~Instructions[7], T2);  // AND_Gate
  assign MUXC = and_47_out ? 1'b0 : 1'bz;  // Controlled_Buffer controlled_buffer_51
  and and_47 (and_47_out, D7_D8, Instructions[10], Instructions[7], T2);
  assign MUXC = and_48_out ? 1'b1 : 1'bz;  // Controlled_Buffer controlled_buffer_52
  and and_48 (and_48_out, D11_D12_D13, ~Instructions[10], ~Instructions[7], T2);  // AND_Gate
  assign MUXC = and_49_out ? 1'b1 : 1'bz;  // Controlled_Buffer controlled_buffer_53
  and and_49 (and_49_out, D11_D12_D13, ~Instructions[10], Instructions[7], T3);  // AND_Gate
  assign MUXC = and_50_out ? 1'b1 : 1'bz;  // Controlled_Buffer controlled_buffer_54
  and and_50 (and_50_out, D11_D12_D13, Instructions[10], ~Instructions[7], T2);  // AND_Gate
  assign MUXC = and_51_out ? 1'b0 : 1'bz;  // Controlled_Buffer controlled_buffer_55
  and and_51 (and_51_out, D17, T2);
  or or_8 (or_8_out, T2, T3);
  or or_9 (or_9_out, T2, T3);
  and and_52 (and_52_out, D2, Instructions[10], T2);
  and and_53 (and_53_out, D4, Instructions[10], T3);
  and and_54 (and_54_out, D5_D6_D9_D10, Instructions[10], ~Instructions[7], ~Instructions[4], T2);  // AND_Gate
  and and_55 (and_55_out, D5_D6_D9_D10, Instructions[10], Instructions[7], ~Instructions[4], T2);  // AND_Gate
  and and_56 (and_56_out, D7_D8, Instructions[10], ~Instructions[7], or_8_out);  // AND_Gate
  and and_57 (and_57_out, D7_D8, Instructions[10], Instructions[7], or_9_out);
  or or_10 (or_10_out, and_52_out, and_53_out, and_54_out, and_55_out, and_56_out, or_11_out);
  or or_11 (or_11_out, and_57_out, and_58_out, and_59_out);
  and and_58 (and_58_out, D11_D12_D13, Instructions[10], ~Instructions[7], T2);  // AND_Gate
  and and_59 (and_59_out, D11_D12_D13, Instructions[10], Instructions[7], T2);
  or or_12 (or_12_out, T0, T1);
  Decoder #(.select(2)) decoder_3 (
    .out0(decoder_3_out0), .out1(decoder_3_out1), .out2(or_13_out[1]), .out3(or_13_out[2]),
    .sel(controlled_buffer_56_out));  // open: en
  assign controlled_buffer_56_out = or_10_out ? Instructions[9:8] : 2'bz;  // Controlled_Buffer controlled_buffer_56
  assign PC_AR_SP_regsel = or_12_out ? 3'b001 : 3'bz;  // Controlled_Buffer controlled_buffer_57
  or or_13 (or_13_out[0], decoder_3_out0, decoder_3_out1);
  assign PC_AR_SP_regsel = or_10_out ? or_13_out : 3'bz;  // Controlled_Buffer controlled_buffer_58
  assign PC_AR_SP_regsel = and_60_out ? 3'b100 : 3'bz;  // Controlled_Buffer controlled_buffer_59
  and and_60 (and_60_out, D3, T2);
  assign PC_AR_SP_regsel = and_61_out ? 3'b100 : 3'bz;  // Controlled_Buffer controlled_buffer_60
  and and_61 (and_61_out, D4, T2);
  assign PC_AR_SP_regsel = and_62_out ? 3'b001 : 3'bz;  // Controlled_Buffer controlled_buffer_61
  and and_62 (and_62_out, D14, T2);
  assign PC_AR_SP_regsel = and_63_out ? 3'b001 : 3'bz;  // Controlled_Buffer controlled_buffer_62
  and and_63 (and_63_out, D15, Z_Flag, T2);
  assign PC_AR_SP_regsel = and_64_out ? 3'b001 : 3'bz;  // Controlled_Buffer controlled_buffer_63
  and and_64 (and_64_out, D16, ~Z_Flag, T2);  // AND_Gate
  assign PC_AR_SP_regsel = and_65_out ? 3'b100 : 3'bz;  // Controlled_Buffer controlled_buffer_64
  and and_65 (and_65_out, D17, T2);
  assign PC_AR_SP_regsel = and_66_out ? 3'b001 : 3'bz;  // Controlled_Buffer controlled_buffer_65
  and and_66 (and_66_out, D17, T3);
  assign PC_AR_SP_regsel = and_67_out ? 3'b100 : 3'bz;  // Controlled_Buffer controlled_buffer_66
  and and_67 (and_67_out, D18, T2);
  assign PC_AR_SP_regsel = and_68_out ? 3'b001 : 3'bz;  // Controlled_Buffer controlled_buffer_67
  and and_68 (and_68_out, D18, T3);
  assign PC_AR_SP_funsel = or_14_out ? 2'b10 : 2'bz;  // Controlled_Buffer controlled_buffer_68
  or or_14 (or_14_out, T0, T1);
  assign PC_AR_SP_funsel = and_69_out ? 2'b01 : 2'bz;  // Controlled_Buffer controlled_buffer_69
  and and_69 (and_69_out, D2, Instructions[10], T2);
  assign PC_AR_SP_funsel = and_70_out ? 2'b11 : 2'bz;  // Controlled_Buffer controlled_buffer_70
  and and_70 (and_70_out, D3, T2);
  assign PC_AR_SP_funsel = and_71_out ? 2'b10 : 2'bz;  // Controlled_Buffer controlled_buffer_71
  and and_71 (and_71_out, D4, T2);
  assign PC_AR_SP_funsel = and_72_out ? 2'b01 : 2'bz;  // Controlled_Buffer controlled_buffer_72
  and and_72 (and_72_out, D4, Instructions[10], T3);
  assign PC_AR_SP_funsel = and_73_out ? 2'b01 : 2'bz;  // Controlled_Buffer controlled_buffer_73
  and and_73 (and_73_out, D5_D6_D9_D10, Instructions[10], ~Instructions[7], ~Instructions[4], T2);  // AND_Gate
  assign PC_AR_SP_funsel = and_74_out ? 2'b01 : 2'bz;  // Controlled_Buffer controlled_buffer_74
  and and_74 (and_74_out, D5_D6_D9_D10, Instructions[10], Instructions[7], ~Instructions[4], T2);  // AND_Gate
  assign PC_AR_SP_funsel = and_75_out ? 2'b01 : 2'bz;  // Controlled_Buffer controlled_buffer_75
  and and_75 (and_75_out, D7_D8, Instructions[10], ~Instructions[7], T2);  // AND_Gate
  assign PC_AR_SP_funsel = and_76_out ? 2'b11 : 2'bz;  // Controlled_Buffer controlled_buffer_76
  and and_76 (and_76_out, D7, Instructions[10], ~Instructions[7], T3);  // AND_Gate
  assign PC_AR_SP_funsel = and_77_out ? 2'b10 : 2'bz;  // Controlled_Buffer controlled_buffer_77
  and and_77 (and_77_out, D8, Instructions[10], ~Instructions[7], T3);  // AND_Gate
  assign PC_AR_SP_funsel = and_78_out ? 2'b01 : 2'bz;  // Controlled_Buffer controlled_buffer_78
  and and_78 (and_78_out, D7_D8, Instructions[10], Instructions[7], T2);
  assign PC_AR_SP_funsel = and_79_out ? 2'b11 : 2'bz;  // Controlled_Buffer controlled_buffer_79
  and and_79 (and_79_out, D7, Instructions[10], Instructions[7], T3);
  assign PC_AR_SP_funsel = and_80_out ? 2'b10 : 2'bz;  // Controlled_Buffer controlled_buffer_80
  and and_80 (and_80_out, D8, Instructions[10], Instructions[7], T3);
  assign PC_AR_SP_funsel = and_81_out ? 2'b01 : 2'bz;  // Controlled_Buffer controlled_buffer_81
  and and_81 (and_81_out, D11_D12_D13, Instructions[10], ~Instructions[7], T2);  // AND_Gate
  assign PC_AR_SP_funsel = and_82_out ? 2'b01 : 2'bz;  // Controlled_Buffer controlled_buffer_82
  and and_82 (and_82_out, D11_D12_D13, Instructions[10], Instructions[7], T2);
  assign PC_AR_SP_funsel = and_83_out ? 2'b01 : 2'bz;  // Controlled_Buffer controlled_buffer_83
  and and_83 (and_83_out, D14, T2);
  assign PC_AR_SP_funsel = and_84_out ? 2'b01 : 2'bz;  // Controlled_Buffer controlled_buffer_84
  and and_84 (and_84_out, D15, Z_Flag, T2);
  assign PC_AR_SP_funsel = and_85_out ? 2'b01 : 2'bz;  // Controlled_Buffer controlled_buffer_85
  and and_85 (and_85_out, D16, ~Z_Flag, T2);  // AND_Gate
  assign PC_AR_SP_funsel = and_86_out ? 2'b11 : 2'bz;  // Controlled_Buffer controlled_buffer_86
  and and_86 (and_86_out, D17, T2);
  assign PC_AR_SP_funsel = and_87_out ? 2'b01 : 2'bz;  // Controlled_Buffer controlled_buffer_87
  and and_87 (and_87_out, D17, T3);
  assign PC_AR_SP_funsel = and_88_out ? 2'b10 : 2'bz;  // Controlled_Buffer controlled_buffer_88
  and and_88 (and_88_out, D18, T2);
  assign PC_AR_SP_funsel = and_89_out ? 2'b01 : 2'bz;  // Controlled_Buffer controlled_buffer_89
  and and_89 (and_89_out, D18, T3);
  assign OutCsel = and_90_out ? Instructions[6:5] : 2'bz;  // Controlled_Buffer controlled_buffer_90
  and and_90 (and_90_out, D2, Instructions[7], T2);
  assign OutCsel = and_91_out ? Instructions[6:5] : 2'bz;  // Controlled_Buffer controlled_buffer_91
  and and_91 (and_91_out, D3, Instructions[7], T2);
  assign OutCsel = and_92_out ? Instructions[6:5] : 2'bz;  // Controlled_Buffer controlled_buffer_92
  and and_92 (and_92_out, D5_D6_D9_D10, ~Instructions[10], Instructions[7], ~Instructions[4], T2);  // AND_Gate
  assign OutCsel = and_93_out ? Instructions[6:5] : 2'bz;  // Controlled_Buffer controlled_buffer_93
  and and_93 (and_93_out, D5_D6_D9_D10, Instructions[10], Instructions[7], ~Instructions[4], T2);  // AND_Gate
  assign OutCsel = and_94_out ? Instructions[6:5] : 2'bz;  // Controlled_Buffer controlled_buffer_94
  and and_94 (and_94_out, D7_D8, ~Instructions[10], Instructions[7], T2);  // AND_Gate
  assign OutCsel = and_95_out ? Instructions[6:5] : 2'bz;  // Controlled_Buffer controlled_buffer_95
  and and_95 (and_95_out, D7_D8, Instructions[10], Instructions[7], T2);
  assign OutCsel = and_96_out ? Instructions[6:5] : 2'bz;  // Controlled_Buffer controlled_buffer_96
  and and_96 (and_96_out, D11_D12_D13, ~Instructions[10], Instructions[7], T2);  // AND_Gate
  assign OutCsel = and_97_out ? Instructions[6:5] : 2'bz;  // Controlled_Buffer controlled_buffer_97
  and and_97 (and_97_out, D11_D12_D13, Instructions[10], Instructions[7], T2);
  assign OutCsel = and_98_out ? 2'b00 : 2'bz;  // Controlled_Buffer controlled_buffer_98
  and and_98 (and_98_out, D17, T2);
  or or_15 (or_15_out, T0, T1);
  and and_99 (and_99_out, D0, Instructions[8], T2);
  assign OutDsel = or_15_out ? 2'b00 : 2'bz;  // Controlled_Buffer controlled_buffer_99
  assign OutDsel = and_99_out ? 2'b10 : 2'bz;  // Controlled_Buffer controlled_buffer_100
  assign OutDsel = and_100_out ? 2'b10 : 2'bz;  // Controlled_Buffer controlled_buffer_101
  and and_100 (and_100_out, D1, Instructions[8], T2);
  assign OutDsel = and_101_out ? 2'b11 : 2'bz;  // Controlled_Buffer controlled_buffer_102
  and and_101 (and_101_out, D3, T2);
  assign OutDsel = and_102_out ? 2'b11 : 2'bz;  // Controlled_Buffer controlled_buffer_103
  and and_102 (and_102_out, D4, T3);
  assign OutDsel = and_103_out ? 2'b11 : 2'bz;  // Controlled_Buffer controlled_buffer_104
  and and_103 (and_103_out, D17, T2);
  assign OutDsel = and_104_out ? 2'b11 : 2'bz;  // Controlled_Buffer controlled_buffer_105
  and and_104 (and_104_out, D18, T3);
  and and_105 (and_105_out, D0, ~Instructions[8], T2);  // AND_Gate
  or or_16 (or_16_out, and_105_out, and_106_out);
  and and_106 (and_106_out, D0, Instructions[8], T2);
  and and_107 (and_107_out, D2, ~Instructions[10], T2);  // AND_Gate
  and and_108 (and_108_out, D4, ~Instructions[10], T3);  // AND_Gate
  and and_109 (and_109_out, D5_D6_D9_D10, ~Instructions[10], ~Instructions[7], ~Instructions[4], T2);  // AND_Gate
  and and_110 (and_110_out, D5_D6_D9_D10, ~Instructions[10], Instructions[7], ~Instructions[4], T2);  // AND_Gate
  and and_111 (and_111_out, D5_D6_D9_D10, ~Instructions[10], Instructions[7], ~Instructions[4], T3);  // AND_Gate
  and and_112 (and_112_out, D7_D8, ~Instructions[10], ~Instructions[7], or_17_out);  // AND_Gate
  or or_17 (or_17_out, T2, T3);
  and and_113 (and_113_out, D7_D8, ~Instructions[10], Instructions[7], or_18_out);  // AND_Gate
  or or_18 (or_18_out, T2, T3);
  and and_114 (and_114_out, D11_D12_D13, ~Instructions[10], ~Instructions[7], T2);  // AND_Gate
  and and_115 (and_115_out, D11_D12_D13, ~Instructions[10], Instructions[7], T2);  // AND_Gate
  and and_116 (and_116_out, D11_D12_D13, ~Instructions[10], Instructions[7], T3);  // AND_Gate
  and and_117 (and_117_out, D17, T2);
  assign controlled_buffer_106_out = or_16_out ? Instructions[10:9] : 2'bz;  // Controlled_Buffer controlled_buffer_106
  assign controlled_buffer_106_out = and_107_out ? Instructions[9:8] : 2'bz;  // Controlled_Buffer controlled_buffer_107
  assign controlled_buffer_106_out = and_108_out ? Instructions[9:8] : 2'bz;  // Controlled_Buffer controlled_buffer_108
  assign controlled_buffer_106_out = and_109_out ? Instructions[9:8] : 2'bz;  // Controlled_Buffer controlled_buffer_109
  assign controlled_buffer_106_out = and_110_out ? Instructions[9:8] : 2'bz;  // Controlled_Buffer controlled_buffer_110
  assign controlled_buffer_106_out = and_111_out ? Instructions[9:8] : 2'bz;  // Controlled_Buffer controlled_buffer_111
  assign controlled_buffer_106_out = and_112_out ? Instructions[9:8] : 2'bz;  // Controlled_Buffer controlled_buffer_112
  assign controlled_buffer_106_out = and_113_out ? Instructions[9:8] : 2'bz;  // Controlled_Buffer controlled_buffer_113
  assign controlled_buffer_106_out = and_114_out ? Instructions[9:8] : 2'bz;  // Controlled_Buffer controlled_buffer_114
  assign controlled_buffer_106_out = and_115_out ? Instructions[9:8] : 2'bz;  // Controlled_Buffer controlled_buffer_115
  assign controlled_buffer_106_out = and_116_out ? Instructions[9:8] : 2'bz;  // Controlled_Buffer controlled_buffer_116
  assign controlled_buffer_106_out = and_117_out ? 2'b11 : 2'bz;  // Controlled_Buffer controlled_buffer_117
  Decoder #(.select(2), .enable("false")) decoder_4 (
    .out0(R0_R3_regsel[0]), .out1(R0_R3_regsel[1]), .out2(R0_R3_regsel[2]), .out3(R0_R3_regsel[3]),
    .sel(controlled_buffer_106_out));
  and and_118 (and_118_out, D0, ~Instructions[8], T2);  // AND_Gate
  and and_119 (and_119_out, D0, Instructions[8], T2);
  and and_120 (and_120_out, D5_D6_D9_D10, ~Instructions[10], Instructions[7], ~Instructions[4], T3);  // AND_Gate
  and and_121 (and_121_out, D7_D8, ~Instructions[10], ~Instructions[7], T2);  // AND_Gate
  and and_122 (and_122_out, D7, ~Instructions[10], ~Instructions[7], T3);  // AND_Gate
  and and_123 (and_123_out, D8, ~Instructions[10], ~Instructions[7], T3);  // AND_Gate
  and and_124 (and_124_out, D7_D8, ~Instructions[10], Instructions[7], T2);  // AND_Gate
  and and_125 (and_125_out, D7, ~Instructions[10], Instructions[7], T3);  // AND_Gate
  and and_126 (and_126_out, D8, ~Instructions[10], Instructions[7], T3);  // AND_Gate
  and and_127 (and_127_out, D11_D12_D13, ~Instructions[10], ~Instructions[7], T2);  // AND_Gate
  and and_128 (and_128_out, D11_D12_D13, ~Instructions[10], Instructions[7], T2);  // AND_Gate
  and and_129 (and_129_out, D11_D12_D13, ~Instructions[10], Instructions[7], T3);  // AND_Gate
  assign R0_R3_funsel = or_19_out ? 2'b01 : 2'bz;  // Controlled_Buffer controlled_buffer_118
  or or_19 (or_19_out, and_118_out, and_119_out);
  assign R0_R3_funsel = and_130_out ? 2'b01 : 2'bz;  // Controlled_Buffer controlled_buffer_119
  and and_130 (and_130_out, D2, ~Instructions[10], T2);  // AND_Gate
  assign R0_R3_funsel = and_131_out ? 2'b01 : 2'bz;  // Controlled_Buffer controlled_buffer_120
  and and_131 (and_131_out, D4, ~Instructions[10], T3);  // AND_Gate
  assign R0_R3_funsel = and_132_out ? 2'b01 : 2'bz;  // Controlled_Buffer controlled_buffer_121
  and and_132 (and_132_out, D5_D6_D9_D10, ~Instructions[10], ~Instructions[7], ~Instructions[4], T2);  // AND_Gate
  assign R0_R3_funsel = and_133_out ? 2'b01 : 2'bz;  // Controlled_Buffer controlled_buffer_122
  and and_133 (and_133_out, D5_D6_D9_D10, ~Instructions[10], Instructions[7], ~Instructions[4], T2);  // AND_Gate
  assign R0_R3_funsel = and_120_out ? 2'b01 : 2'bz;  // Controlled_Buffer controlled_buffer_123
  assign R0_R3_funsel = and_121_out ? 2'b01 : 2'bz;  // Controlled_Buffer controlled_buffer_124
  assign R0_R3_funsel = and_122_out ? 2'b11 : 2'bz;  // Controlled_Buffer controlled_buffer_125
  assign R0_R3_funsel = and_123_out ? 2'b10 : 2'bz;  // Controlled_Buffer controlled_buffer_126
  assign R0_R3_funsel = and_124_out ? 2'b01 : 2'bz;  // Controlled_Buffer controlled_buffer_127
  assign R0_R3_funsel = and_125_out ? 2'b11 : 2'bz;  // Controlled_Buffer controlled_buffer_128
  assign R0_R3_funsel = and_126_out ? 2'b10 : 2'bz;  // Controlled_Buffer controlled_buffer_129
  assign R0_R3_funsel = and_127_out ? 2'b01 : 2'bz;  // Controlled_Buffer controlled_buffer_130
  assign R0_R3_funsel = and_128_out ? 2'b01 : 2'bz;  // Controlled_Buffer controlled_buffer_131
  assign R0_R3_funsel = and_129_out ? 2'b01 : 2'bz;  // Controlled_Buffer controlled_buffer_132
  assign OutAsel = and_134_out ? Instructions[6:5] : 2'bz;  // Controlled_Buffer controlled_buffer_133
  and and_134 (and_134_out, D5_D6_D9_D10, ~Instructions[10], ~Instructions[7], ~Instructions[4], T2);  // AND_Gate
  assign OutAsel = and_135_out ? Instructions[9:8] : 2'bz;  // Controlled_Buffer controlled_buffer_134
  and and_135 (and_135_out, D5_D6_D9_D10, ~Instructions[10], Instructions[7], ~Instructions[4], T2);  // AND_Gate
  assign OutAsel = and_136_out ? Instructions[6:5] : 2'bz;  // Controlled_Buffer controlled_buffer_135
  and and_136 (and_136_out, D5_D6_D9_D10, Instructions[10], ~Instructions[7], ~Instructions[4], T2);  // AND_Gate
  assign OutAsel = and_137_out ? Instructions[6:5] : 2'bz;  // Controlled_Buffer controlled_buffer_136
  and and_137 (and_137_out, D7_D8, ~Instructions[10], ~Instructions[7], T2);  // AND_Gate
  assign OutAsel = and_138_out ? Instructions[6:5] : 2'bz;  // Controlled_Buffer controlled_buffer_137
  and and_138 (and_138_out, D7_D8, Instructions[10], ~Instructions[7], T2);  // AND_Gate
  assign OutAsel = and_139_out ? Instructions[6:5] : 2'bz;  // Controlled_Buffer controlled_buffer_138
  and and_139 (and_139_out, D11_D12_D13, ~Instructions[10], ~Instructions[7], T2);  // AND_Gate
  assign OutAsel = and_140_out ? Instructions[9:8] : 2'bz;  // Controlled_Buffer controlled_buffer_139
  and and_140 (and_140_out, D11_D12_D13, ~Instructions[10], Instructions[7], T3);  // AND_Gate
  assign OutAsel = and_141_out ? Instructions[6:5] : 2'bz;  // Controlled_Buffer controlled_buffer_140
  and and_141 (and_141_out, D11_D12_D13, Instructions[10], ~Instructions[7], T2);  // AND_Gate
  and and_142 (and_142_out, D3, ~Instructions[7], T2);  // AND_Gate
  and and_143 (and_143_out, D5_D6_D9_D10, ~Instructions[10], ~Instructions[7], ~Instructions[4], T2);  // AND_Gate
  and and_144 (and_144_out, D5_D6_D9_D10, ~Instructions[10], Instructions[7], ~Instructions[4], T3);  // AND_Gate
  and and_145 (and_145_out, D5_D6_D9_D10, Instructions[10], ~Instructions[7], ~Instructions[4], T2);  // AND_Gate
  and and_146 (and_146_out, D5_D6_D9_D10, Instructions[10], Instructions[7], ~Instructions[4], T2);  // AND_Gate
  assign OutBsel = and_147_out ? Instructions[10:9] : 2'bz;  // Controlled_Buffer controlled_buffer_141
  and and_147 (and_147_out, D1, Instructions[8], T2);
  assign OutBsel = and_148_out ? Instructions[6:5] : 2'bz;  // Controlled_Buffer controlled_buffer_142
  and and_148 (and_148_out, D2, ~Instructions[7], T2);  // AND_Gate
  assign OutBsel = and_142_out ? Instructions[6:5] : 2'bz;  // Controlled_Buffer controlled_buffer_143
  assign OutBsel = and_143_out ? Instructions[3:2] : 2'bz;  // Controlled_Buffer controlled_buffer_144
  assign OutBsel = and_144_out ? Instructions[3:2] : 2'bz;  // Controlled_Buffer controlled_buffer_145
  assign OutBsel = and_145_out ? Instructions[3:2] : 2'bz;  // Controlled_Buffer controlled_buffer_146
  assign OutBsel = and_146_out ? Instructions[3:2] : 2'bz;  // Controlled_Buffer controlled_buffer_147
  assign Alu_Funsel = and_149_out ? 4'b0001 : 4'bz;  // Controlled_Buffer controlled_buffer_148
  and and_149 (and_149_out, D1, Instructions[8], T2);
  assign Alu_Funsel = and_150_out ? 4'b0000 : 4'bz;  // Controlled_Buffer controlled_buffer_149
  and and_150 (and_150_out, D2, Instructions[10], Instructions[7], T2);
  assign Alu_Funsel = and_151_out ? 4'b0001 : 4'bz;  // Controlled_Buffer controlled_buffer_150
  and and_151 (and_151_out, D2, ~Instructions[7], T2);  // AND_Gate
  assign Alu_Funsel = and_152_out ? 4'b0001 : 4'bz;  // Controlled_Buffer controlled_buffer_151
  and and_152 (and_152_out, D3, ~Instructions[7], T2);  // AND_Gate
  assign Alu_Funsel = and_153_out ? 4'b0000 : 4'bz;  // Controlled_Buffer controlled_buffer_152
  and and_153 (and_153_out, D3, Instructions[7], T2);
  assign Alu_Funsel = and_154_out ? 4'b0100 : 4'bz;  // Controlled_Buffer controlled_buffer_153
  and and_154 (and_154_out, D5, ~Instructions[10], ~Instructions[7], ~Instructions[4], T2);  // AND_Gate
  assign Alu_Funsel = and_155_out ? 4'b0100 : 4'bz;  // Controlled_Buffer controlled_buffer_154
  and and_155 (and_155_out, D5, ~Instructions[10], Instructions[7], ~Instructions[4], T3);  // AND_Gate
  assign Alu_Funsel = and_156_out ? 4'b0100 : 4'bz;  // Controlled_Buffer controlled_buffer_155
  and and_156 (and_156_out, D5, Instructions[10], ~Instructions[4], T2);  // AND_Gate
  assign Alu_Funsel = and_157_out ? 4'b0110 : 4'bz;  // Controlled_Buffer controlled_buffer_156
  and and_157 (and_157_out, D6, ~Instructions[10], ~Instructions[7], ~Instructions[4], T2);  // AND_Gate
  assign Alu_Funsel = and_158_out ? 4'b0110 : 4'bz;  // Controlled_Buffer controlled_buffer_157
  and and_158 (and_158_out, D6, ~Instructions[10], Instructions[7], ~Instructions[4], T3);  // AND_Gate
  assign Alu_Funsel = and_159_out ? 4'b0110 : 4'bz;  // Controlled_Buffer controlled_buffer_158
  and and_159 (and_159_out, D6, Instructions[10], ~Instructions[4], T2);  // AND_Gate
  assign Alu_Funsel = and_160_out ? 4'b0111 : 4'bz;  // Controlled_Buffer controlled_buffer_159
  and and_160 (and_160_out, D9, ~Instructions[10], ~Instructions[7], ~Instructions[4], T2);  // AND_Gate
  assign Alu_Funsel = and_161_out ? 4'b0111 : 4'bz;  // Controlled_Buffer controlled_buffer_160
  and and_161 (and_161_out, D9, ~Instructions[10], Instructions[7], ~Instructions[4], T3);  // AND_Gate
  assign Alu_Funsel = and_162_out ? 4'b0111 : 4'bz;  // Controlled_Buffer controlled_buffer_161
  and and_162 (and_162_out, D9, Instructions[10], ~Instructions[4], T2);  // AND_Gate
  assign Alu_Funsel = and_163_out ? 4'b1000 : 4'bz;  // Controlled_Buffer controlled_buffer_162
  and and_163 (and_163_out, D10, ~Instructions[10], ~Instructions[7], ~Instructions[4], T2);  // AND_Gate
  assign Alu_Funsel = and_164_out ? 4'b1000 : 4'bz;  // Controlled_Buffer controlled_buffer_163
  and and_164 (and_164_out, D10, ~Instructions[10], Instructions[7], ~Instructions[4], T3);  // AND_Gate
  assign Alu_Funsel = and_165_out ? 4'b1000 : 4'bz;  // Controlled_Buffer controlled_buffer_164
  and and_165 (and_165_out, D10, Instructions[10], ~Instructions[4], T2);  // AND_Gate
  assign Alu_Funsel = and_166_out ? 4'b0000 : 4'bz;  // Controlled_Buffer controlled_buffer_165
  and and_166 (and_166_out, D7_D8, ~Instructions[10], ~Instructions[7], T2);  // AND_Gate
  assign Alu_Funsel = and_167_out ? 4'b0000 : 4'bz;  // Controlled_Buffer controlled_buffer_166
  and and_167 (and_167_out, D7_D8, Instructions[10], ~Instructions[7], T2);  // AND_Gate
  assign Alu_Funsel = and_168_out ? 4'b0000 : 4'bz;  // Controlled_Buffer controlled_buffer_167
  and and_168 (and_168_out, D7_D8, Instructions[10], Instructions[7], T2);
  assign Alu_Funsel = and_169_out ? 4'b0010 : 4'bz;  // Controlled_Buffer controlled_buffer_168
  and and_169 (and_169_out, D11, ~Instructions[10], ~Instructions[7], T2);  // AND_Gate
  assign Alu_Funsel = and_170_out ? 4'b0010 : 4'bz;  // Controlled_Buffer controlled_buffer_169
  and and_170 (and_170_out, D11, ~Instructions[10], Instructions[7], T3);  // AND_Gate
  assign Alu_Funsel = and_171_out ? 4'b0010 : 4'bz;  // Controlled_Buffer controlled_buffer_170
  and and_171 (and_171_out, D11, Instructions[10], T2);
  assign Alu_Funsel = and_172_out ? 4'b1010 : 4'bz;  // Controlled_Buffer controlled_buffer_171
  and and_172 (and_172_out, D12, ~Instructions[10], ~Instructions[7], T2);  // AND_Gate
  assign Alu_Funsel = and_173_out ? 4'b1010 : 4'bz;  // Controlled_Buffer controlled_buffer_172
  and and_173 (and_173_out, D12, ~Instructions[10], Instructions[7], T3);  // AND_Gate
  assign Alu_Funsel = and_174_out ? 4'b1010 : 4'bz;  // Controlled_Buffer controlled_buffer_173
  and and_174 (and_174_out, D12, Instructions[10], T2);
  assign Alu_Funsel = and_175_out ? 4'b1011 : 4'bz;  // Controlled_Buffer controlled_buffer_174
  and and_175 (and_175_out, D13, ~Instructions[10], ~Instructions[7], T2);  // AND_Gate
  assign Alu_Funsel = and_176_out ? 4'b1011 : 4'bz;  // Controlled_Buffer controlled_buffer_175
  and and_176 (and_176_out, D13, ~Instructions[10], Instructions[7], T3);  // AND_Gate
  assign Alu_Funsel = and_177_out ? 4'b1011 : 4'bz;  // Controlled_Buffer controlled_buffer_176
  and and_177 (and_177_out, D13, Instructions[10], T2);
  assign Alu_Funsel = and_178_out ? 4'b0000 : 4'bz;  // Controlled_Buffer controlled_buffer_177
  and and_178 (and_178_out, D17, T2);
  and and_179 (and_179_out, D0, Instructions[8], T2);
  or or_20 (or_20_out, and_179_out, and_180_out);
  and and_180 (and_180_out, D0, ~Instructions[8], T2);  // AND_Gate
  and and_181 (and_181_out, D1, T2);
  and and_182 (and_182_out, D2, T2);
  and and_183 (and_183_out, D3, T2);
  and and_184 (and_184_out, D4, T3);
  and and_185 (and_185_out, D5_D6_D9_D10, ~Instructions[10], ~Instructions[7], ~Instructions[4], T2);  // AND_Gate
  and and_186 (and_186_out, D5_D6_D9_D10, ~Instructions[10], Instructions[7], ~Instructions[4], T3);  // AND_Gate
  and and_187 (and_187_out, D15, Z_Flag, T2);
  and and_188 (and_188_out, D16, ~Z_Flag, T2);  // AND_Gate
  and and_189 (and_189_out, D18, T3);
  assign Time_Reset = or_20_out ? 1'b1 : 1'bz;  // Controlled_Buffer controlled_buffer_178
  assign Time_Reset = and_181_out ? 1'b1 : 1'bz;  // Controlled_Buffer controlled_buffer_179
  assign Time_Reset = and_182_out ? 1'b1 : 1'bz;  // Controlled_Buffer controlled_buffer_180
  assign Time_Reset = and_183_out ? 1'b1 : 1'bz;  // Controlled_Buffer controlled_buffer_181
  assign Time_Reset = and_184_out ? 1'b1 : 1'bz;  // Controlled_Buffer controlled_buffer_182
  assign Time_Reset = and_185_out ? 1'b1 : 1'bz;  // Controlled_Buffer controlled_buffer_183
  assign Time_Reset = and_186_out ? 1'b1 : 1'bz;  // Controlled_Buffer controlled_buffer_184
  assign Time_Reset = and_190_out ? 1'b1 : 1'bz;  // Controlled_Buffer controlled_buffer_185
  and and_190 (and_190_out, D5_D6_D9_D10, Instructions[10], ~Instructions[7], ~Instructions[4], T2);  // AND_Gate
  assign Time_Reset = and_191_out ? 1'b1 : 1'bz;  // Controlled_Buffer controlled_buffer_186
  and and_191 (and_191_out, D5_D6_D9_D10, Instructions[10], Instructions[7], ~Instructions[4], T2);  // AND_Gate
  assign Time_Reset = and_192_out ? 1'b1 : 1'bz;  // Controlled_Buffer controlled_buffer_187
  and and_192 (and_192_out, D7_D8, ~Instructions[10], ~Instructions[7], T3);  // AND_Gate
  assign Time_Reset = and_193_out ? 1'b1 : 1'bz;  // Controlled_Buffer controlled_buffer_188
  and and_193 (and_193_out, D7_D8, ~Instructions[10], Instructions[7], T3);  // AND_Gate
  assign Time_Reset = and_194_out ? 1'b1 : 1'bz;  // Controlled_Buffer controlled_buffer_189
  and and_194 (and_194_out, D7_D8, Instructions[10], ~Instructions[7], T3);  // AND_Gate
  assign Time_Reset = and_195_out ? 1'b1 : 1'bz;  // Controlled_Buffer controlled_buffer_190
  and and_195 (and_195_out, D7_D8, Instructions[10], Instructions[7], T3);
  assign Time_Reset = and_196_out ? 1'b1 : 1'bz;  // Controlled_Buffer controlled_buffer_191
  and and_196 (and_196_out, D11_D12_D13, ~Instructions[10], ~Instructions[7], T2);  // AND_Gate
  assign Time_Reset = and_197_out ? 1'b1 : 1'bz;  // Controlled_Buffer controlled_buffer_192
  and and_197 (and_197_out, D11_D12_D13, ~Instructions[10], Instructions[7], T3);  // AND_Gate
  assign Time_Reset = and_198_out ? 1'b1 : 1'bz;  // Controlled_Buffer controlled_buffer_193
  and and_198 (and_198_out, D11_D12_D13, Instructions[10], T2);
  assign Time_Reset = and_199_out ? 1'b1 : 1'bz;  // Controlled_Buffer controlled_buffer_194
  and and_199 (and_199_out, D14, T2);
  assign Time_Reset = and_187_out ? 1'b1 : 1'bz;  // Controlled_Buffer controlled_buffer_195
  assign Time_Reset = and_188_out ? 1'b1 : 1'bz;  // Controlled_Buffer controlled_buffer_196
  assign Time_Reset = and_200_out ? 1'b1 : 1'bz;  // Controlled_Buffer controlled_buffer_197
  and and_200 (and_200_out, D17, T3);
  assign Time_Reset = and_189_out ? 1'b1 : 1'bz;  // Controlled_Buffer controlled_buffer_198

  // Other names for the same wires on the sheet: IR11 = Instructions[11]; IR12 = Instructions[12];
  //   IR13 = Instructions[13]; IR14 = Instructions[14]; IR15 = Instructions[15]; IR8 = Instructions[8];
  //   IR5 = Instructions[5]; IR6 = Instructions[6]; IR2 = Instructions[2]; IR3 = Instructions[3];
  //   IR9 = Instructions[9]; IR10 = Instructions[10]; IR0 = Instructions[0]; IR1 = Instructions[1];
  //   IR4 = Instructions[4]; IR7 = Instructions[7]; IR_L_H_prime = L_H_prime;
  //   PC_AR_SP_PC_FUNSEL[1:0] = PC_AR_SP_funsel; PC_AR_SP_PC_OUTCSEL[1:0] = OutCsel;
  //   PC_AR_SP_PC_OUTDSEL[1:0] = OutDsel; PC_AR_SP_PC_REGSEL[2:0] = PC_AR_SP_regsel;
  //   R0_R1_R2_R3_FUNSEL[1:0] = R0_R3_funsel; R0_R1_R2_R3_OUTASEL[1:0] = OutAsel; R0_R1_R2_R3_OUTBSEL[1:0] = OutBsel;
  //   R0_R1_R2_R3_REGSEL[3:0] = R0_R3_regsel; Z = Z_Flag
endmodule
