// Logisim project circ shift right.circ as structural Verilog: 1 circuit, main circuit main
module main (
  input  [7:0] INPUT,
  output CARRY,
  output [7:0] OUTPUT,
  output OVERFLOW
);

  xor xor_1 (OVERFLOW, INPUT[0], INPUT[7]);

  assign CARRY = INPUT[0];
  assign OUTPUT = {INPUT[0], INPUT[7:1]};
endmodule
