// Logisim project part1-16bit.circ as structural Verilog: 1 circuit, main circuit main
module main (
  input  CLK__do_not_use,
  input  [15:0] \Input_Pın___16_bit ,
  input  [1:0] FunSel,
  input  ENABLE,
  output [15:0] out_5,
  output out_6
);

  wire and_1_out, and_2_out, and_3_out, and_4_out, and_5_out, and_6_out, and_7_out, and_8_out, and_9_out,
       and_10_out, and_11_out, and_12_out, and_13_out, and_14_out, and_15_out, and_16_out, and_17_out,
       and_18_out, and_19_out, and_20_out, and_21_out, and_22_out, and_23_out, and_24_out, and_25_out,
       and_26_out, and_27_out, and_28_out, and_29_out, and_30_out, and_31_out, and_32_out, and_33_out,
       and_34_out, CLK_out, decoder_1_out0, decoder_1_out1, decoder_1_out2, decoder_1_out3, or_1_out,
       or_2_out, or_3_out, or_4_out, or_5_out, or_6_out, or_7_out, or_8_out, or_9_out, or_10_out, or_11_out,
       or_12_out, or_13_out, or_14_out, or_15_out, or_16_out, or_17_out, or_18_out, or_19_out;
  wire [15:0] adder_1_out, multiplexer_1_out;

  Decoder #(.select(2), .enable("false")) decoder_1 (
    .out0(decoder_1_out0), .out1(decoder_1_out1), .out2(decoder_1_out2), .out3(decoder_1_out3), .sel(FunSel));
  Hex_Digit_Display hex_digit_display_1 (.value(\Input_Pın___16_bit [15:12]));  // open: dp
  or or_1 (or_1_out, decoder_1_out2, decoder_1_out3);
  Hex_Digit_Display hex_digit_display_2 (.value(\Input_Pın___16_bit [7:4]));  // open: dp
  Hex_Digit_Display hex_digit_display_3 (.value(\Input_Pın___16_bit [11:8]));  // open: dp
  Hex_Digit_Display hex_digit_display_4 (.value(\Input_Pın___16_bit [3:0]));  // open: dp
  and and_1 (and_1_out, \Input_Pın___16_bit [15], decoder_1_out1);
  and and_2 (and_2_out, \Input_Pın___16_bit [14], decoder_1_out1);
  and and_3 (and_3_out, \Input_Pın___16_bit [13], decoder_1_out1);
  and and_4 (and_4_out, \Input_Pın___16_bit [12], decoder_1_out1);
  and and_5 (and_5_out, \Input_Pın___16_bit [11], decoder_1_out1);
  and and_6 (and_6_out, \Input_Pın___16_bit [10], decoder_1_out1);
  and and_7 (and_7_out, \Input_Pın___16_bit [9], decoder_1_out1);
  and and_8 (and_8_out, \Input_Pın___16_bit [8], decoder_1_out1);
  and and_9 (and_9_out, \Input_Pın___16_bit [7], decoder_1_out1);
  and and_10 (and_10_out, \Input_Pın___16_bit [6], decoder_1_out1);
  and and_11 (and_11_out, \Input_Pın___16_bit [5], decoder_1_out1);
  and and_12 (and_12_out, \Input_Pın___16_bit [4], decoder_1_out1);
  and and_13 (and_13_out, \Input_Pın___16_bit [3], decoder_1_out1);
  and and_14 (and_14_out, \Input_Pın___16_bit [2], decoder_1_out1);
  and and_15 (and_15_out, \Input_Pın___16_bit [1], decoder_1_out1);
  and and_16 (and_16_out, \Input_Pın___16_bit [0], decoder_1_out1);
  Clock CLK (.out(CLK_out));
  or or_2 (or_2_out, CLK__do_not_use, CLK_out);
  or or_3 (or_3_out, and_1_out, and_17_out);
  and and_17 (and_17_out, adder_1_out[15], or_1_out);
  or or_4 (or_4_out, and_2_out, and_18_out);
  and and_18 (and_18_out, adder_1_out[14], or_1_out);
  or or_5 (or_5_out, and_3_out, and_19_out);
  and and_19 (and_19_out, adder_1_out[13], or_1_out);
  or or_6 (or_6_out, and_4_out, and_20_out);
  and and_20 (and_20_out, adder_1_out[12], or_1_out);
  or or_7 (or_7_out, and_5_out, and_21_out);
  and and_21 (and_21_out, adder_1_out[11], or_1_out);
  or or_8 (or_8_out, and_6_out, and_22_out);
  and and_22 (and_22_out, adder_1_out[10], or_1_out);
  or or_9 (or_9_out, and_7_out, and_23_out);
  and and_23 (and_23_out, adder_1_out[9], or_1_out);
  or or_10 (or_10_out, and_8_out, and_24_out);
  and and_24 (and_24_out, adder_1_out[8], or_1_out);
  or or_11 (or_11_out, and_9_out, and_25_out);
  and and_25 (and_25_out, adder_1_out[7], or_1_out);
  or or_12 (or_12_out, and_10_out, and_26_out);
  and and_26 (and_26_out, adder_1_out[6], or_1_out);
  or or_13 (or_13_out, and_11_out, and_27_out);
  and and_27 (and_27_out, adder_1_out[5], or_1_out);
  or or_14 (or_14_out, and_12_out, and_28_out);
  and and_28 (and_28_out, adder_1_out[4], or_1_out);
  or or_15 (or_15_out, and_13_out, and_29_out);
  and and_29 (and_29_out, adder_1_out[3], or_1_out);
  or or_16 (or_16_out, and_14_out, and_30_out);
  and and_30 (and_30_out, adder_1_out[2], or_1_out);
  or or_17 (or_17_out, and_15_out, and_31_out);
  and and_31 (and_31_out, adder_1_out[1], or_1_out);
  or or_18 (or_18_out, and_16_out, and_32_out);
  and and_32 (and_32_out, adder_1_out[0], or_1_out);
  D_Flip_Flop d_ff_1 (
    .clk(or_2_out), .D(or_3_out), .Q(out_5[15]), .en(ENABLE), .reset(and_33_out));  // open: Qn, preset
  D_Flip_Flop d_ff_2 (
    .clk(or_2_out), .D(or_4_out), .Q(out_5[14]), .en(ENABLE), .reset(and_33_out));  // open: Qn, preset
  D_Flip_Flop d_ff_3 (
    .clk(or_2_out), .D(or_5_out), .Q(out_5[13]), .en(ENABLE), .reset(and_33_out));  // open: Qn, preset
  D_Flip_Flop d_ff_4 (
    .clk(or_2_out), .D(or_6_out), .Q(out_5[12]), .en(ENABLE), .reset(and_33_out));  // open: Qn, preset
  D_Flip_Flop d_ff_5 (
    .clk(or_2_out), .D(or_7_out), .Q(out_5[11]), .en(ENABLE), .reset(and_33_out));  // open: Qn, preset
  D_Flip_Flop d_ff_6 (
    .clk(or_2_out), .D(or_8_out), .Q(out_5[10]), .en(ENABLE), .reset(and_33_out));  // open: Qn, preset
  D_Flip_Flop d_ff_7 (.clk(or_2_out), .D(or_9_out), .Q(out_5[9]), .en(ENABLE), .reset(and_33_out));  // open: Qn, preset
  D_Flip_Flop d_ff_8 (
    .clk(or_2_out), .D(or_10_out), .Q(out_5[8]), .en(ENABLE), .reset(and_33_out));  // open: Qn, preset
  D_Flip_Flop d_ff_9 (
    .clk(or_2_out), .D(or_11_out), .Q(out_5[7]), .en(ENABLE), .reset(and_33_out));  // open: Qn, preset
  D_Flip_Flop d_ff_10 (
    .clk(or_2_out), .D(or_12_out), .Q(out_5[6]), .en(ENABLE), .reset(and_33_out));  // open: Qn, preset
  D_Flip_Flop d_ff_11 (
    .clk(or_2_out), .D(or_13_out), .Q(out_5[5]), .en(ENABLE), .reset(and_33_out));  // open: Qn, preset
  D_Flip_Flop d_ff_12 (
    .clk(or_2_out), .D(or_14_out), .Q(out_5[4]), .en(ENABLE), .reset(and_33_out));  // open: Qn, preset
  D_Flip_Flop d_ff_13 (
    .clk(or_2_out), .D(or_15_out), .Q(out_5[3]), .en(ENABLE), .reset(and_33_out));  // open: Qn, preset
  D_Flip_Flop d_ff_14 (
    .clk(or_2_out), .D(or_16_out), .Q(out_5[2]), .en(ENABLE), .reset(and_33_out));  // open: Qn, preset
  D_Flip_Flop d_ff_15 (
    .clk(or_2_out), .D(or_17_out), .Q(out_5[1]), .en(ENABLE), .reset(and_33_out));  // open: Qn, preset
  D_Flip_Flop d_ff_16 (
    .clk(or_2_out), .D(or_18_out), .Q(out_5[0]), .en(ENABLE), .reset(and_33_out));  // open: Qn, preset
  and and_33 (and_33_out, ENABLE, and_34_out);
  and and_34 (and_34_out, or_2_out, decoder_1_out0);
  Multiplexer #(.width(16)) multiplexer_1 (
    .in0({16{1'b1}}), .in1(16'h1), .out(multiplexer_1_out), .sel(decoder_1_out2), .en(or_19_out));
  or or_19 (or_19_out, decoder_1_out2, decoder_1_out3);
  Adder #(.width(16)) adder_1 (.a(out_5), .b(multiplexer_1_out), .out(adder_1_out), .cout(out_6));  // open: cin
  Hex_Digit_Display hex_digit_display_5 (.value(out_5[11:8]));  // open: dp
  Hex_Digit_Display hex_digit_display_6 (.value(out_5[15:12]));  // open: dp
  Hex_Digit_Display hex_digit_display_7 (.value(out_5[3:0]));  // open: dp
  Hex_Digit_Display hex_digit_display_8 (.value(out_5[7:4]));  // open: dp

  // Notes on the sheet:
  //   16-bit Hexadecimal Output
  //   16-bit Hexadecimal Output
endmodule
