// Logisim project part1log.circ as structural Verilog: 1 circuit, main circuit main
module main (
  input  a,
  input  b,
  input  c,
  input  d
);

  wire and_1_out, and_2_out, and_3_out, and_4_out, not_1_out, not_2_out, not_3_out, or_1_out;

  not not_1 (not_1_out, a);
  not not_2 (not_2_out, b);
  not not_3 (not_3_out, c);
  and and_1 (and_1_out, not_1_out, not_2_out, not_3_out);
  and and_2 (and_2_out, c, d);
  and and_3 (and_3_out, not_2_out, d);
  and and_4 (and_4_out, a, b, not_3_out);
  LED led_1 (.in(or_1_out));
  or or_1 (or_1_out, and_1_out, and_2_out, and_3_out, and_4_out);
  LED led_2 (.in(or_1_out));

  // Notes on the sheet:
  //   LED Monitors
  //   High
  //   Low
endmodule
