// Logisim project part3log.circ as structural Verilog: 1 circuit, main circuit main
module main (
  input  a,
  input  b,
  input  c,
  input  d
);

  wire multiplexer_1_out;

  Multiplexer #(.select(3), .enable("false")) multiplexer_1 (
    .in0(1'b1), .in1(d), .in2(d), .in3(d), .in4(1'b0), .in5(d), .in6(1'b1), .in7(d), .out(multiplexer_1_out),
    .sel({a, b, c}));
  LED led_1 (.in(multiplexer_1_out));
  LED led_2 (.in(multiplexer_1_out));

  // Notes on the sheet:
  //   0
  //   1
  //   Logic Monitors
  //   High
  //   Low
endmodule
