// Logisim project part4log1.circ as structural Verilog: 1 circuit, main circuit main
module main (
  input  a,
  input  b,
  input  c
);

  wire decoder_1_out0, decoder_1_out2, decoder_1_out3, decoder_1_out7, not_1_out, not_2_out, not_3_out,
       not_4_out, or_1_out, or_2_out, or_3_out;

  Decoder #(.select(3), .enable("false")) decoder_1 (
    .out0(decoder_1_out0), .out2(decoder_1_out2), .out3(decoder_1_out3), .out7(decoder_1_out7),
    .sel({a, b, c}));  // open: out1, out4, out5, out6
  not not_1 (not_1_out, decoder_1_out0);
  not not_2 (not_2_out, decoder_1_out2);
  not not_3 (not_3_out, decoder_1_out3);
  not not_4 (not_4_out, decoder_1_out7);
  or or_1 (or_1_out, not_1_out, not_2_out);
  or or_2 (or_2_out, not_3_out, not_4_out);
  LED led_1 (.in(or_3_out));
  or or_3 (or_3_out, or_1_out, or_2_out);
  LED led_2 (.in(or_3_out));

  // Notes on the sheet:
  //   Logic Monitors
  //   High
  //   Low
endmodule
